// Logisim project Assignment 2.circ as structural Verilog: 2 circuits, main circuit main
module main (
  input  Subtract,
  input  [3:0] A,
  input  [3:0] B
);

  wire fas_1_carry_out, fas_2_carry_out, fas_3_carry_out, fas_4_carry_out;
  wire [3:0] fas_1_sum;

  fas fas_1 (
    .A(A[0]), .B(B[0]), .Sum(fas_1_sum[0]), .Subtract(Subtract), .Carry_In(Subtract),
    .Carry_out(fas_1_carry_out));
  fas fas_2 (
    .A(A[1]), .B(B[1]), .Sum(fas_1_sum[1]), .Subtract(Subtract), .Carry_In(fas_1_carry_out),
    .Carry_out(fas_2_carry_out));
  fas fas_3 (
    .A(A[2]), .B(B[2]), .Sum(fas_1_sum[2]), .Subtract(Subtract), .Carry_In(fas_2_carry_out),
    .Carry_out(fas_3_carry_out));
  fas fas_4 (
    .A(A[3]), .B(B[3]), .Sum(fas_1_sum[3]), .Subtract(Subtract), .Carry_In(fas_3_carry_out),
    .Carry_out(fas_4_carry_out));
  // Probe on fas_4_carry_out
  // Probe on fas_1_sum
endmodule

module fas (
  input  Subtract,
  input  Carry_In,
  input  A,
  input  B,
  output Sum,
  output Carry_out
);

  wire and_1_out, and_2_out, xor_1_out, xor_2_out;

  xor xor_1 (xor_1_out, Subtract, B);
  and and_1 (and_1_out, xor_1_out, A);
  xor xor_2 (xor_2_out, A, xor_1_out);
  and and_2 (and_2_out, xor_2_out, Carry_In);
  or or_1 (Carry_out, and_1_out, and_2_out);
  xor xor_3 (Sum, Carry_In, xor_2_out);
endmodule
