// Logisim project Assignment 3.circ as structural Verilog: 3 circuits, main circuit main
module main (
  input  write_enable,
  input  select0,
  input  select1,
  input  [2:0] data_in,
  output [2:0] data_out
);

  wire and_1_out, and_2_out, and_3_out, and_4_out, clock_out, decoder_1_output0, decoder_1_output1,
       decoder_1_output2, decoder_1_output3;
  wire [2:0] register_1_q, register_2_q, register_3_q, register_4_q;

  decoder decoder_1 (
    .select0(select0), .select1(select1), .output0(decoder_1_output0), .output1(decoder_1_output1),
    .output2(decoder_1_output2), .output3(decoder_1_output3));
  and and_1 (and_1_out, decoder_1_output0, write_enable);
  and and_2 (and_2_out, decoder_1_output1, write_enable);
  and and_3 (and_3_out, decoder_1_output2, write_enable);
  and and_4 (and_4_out, decoder_1_output3, write_enable);
  Clock clock (.out(clock_out));
  Register #(.width(3)) register_1 (.D(data_in), .en(and_1_out), .Q(register_1_q), .clk(clock_out));  // open: clr
  Register #(.width(3)) register_2 (.D(data_in), .en(and_2_out), .Q(register_2_q), .clk(clock_out));  // open: clr
  Register #(.width(3)) register_3 (.D(data_in), .en(and_3_out), .Q(register_3_q), .clk(clock_out));  // open: clr
  Register #(.width(3)) register_4 (.D(data_in), .en(and_4_out), .Q(register_4_q), .clk(clock_out));  // open: clr
  multiplexer multiplexer_1 (
    .input0(register_1_q[0]), .input1(register_2_q[0]), .input2(register_3_q[0]), .input3(register_4_q[0]),
    .select0(select0), .select1(select1), .\output (data_out[0]));
  multiplexer multiplexer_2 (
    .input0(register_1_q[1]), .input1(register_2_q[1]), .input2(register_3_q[1]), .input3(register_4_q[1]),
    .select0(select0), .select1(select1), .\output (data_out[1]));
  multiplexer multiplexer_3 (
    .input0(register_1_q[2]), .input1(register_2_q[2]), .input2(register_3_q[2]), .input3(register_4_q[2]),
    .select0(select0), .select1(select1), .\output (data_out[2]));
endmodule

module multiplexer (
  input  select0,
  input  select1,
  input  input0,
  input  input1,
  input  input2,
  input  input3,
  output \output 
);

  wire and_1_out, and_2_out, and_3_out, and_4_out, and_5_out, and_6_out, and_7_out, not_1_out, xor_1_out,
       xor_2_out;

  and and_1 (and_1_out, select1, select0);
  not not_1 (not_1_out, and_1_out);
  xor xor_1 (xor_1_out, select0, select1);
  and and_2 (and_2_out, select0, select0, xor_1_out);
  and and_3 (and_3_out, xor_1_out, select1);
  ExactlyOne xor_2 (.out(xor_2_out), .in0(and_3_out), .in2(and_2_out), .in4(not_1_out));
  and and_4 (and_4_out, input0, xor_2_out);
  and and_5 (and_5_out, input1, and_2_out);
  and and_6 (and_6_out, and_3_out, input2);
  and and_7 (and_7_out, and_1_out, input3);
  or or_1 (\output , and_4_out, and_5_out, and_6_out, and_7_out);
endmodule

module decoder (
  input  select0,
  input  select1,
  output output0,
  output output1,
  output output2,
  output output3
);

  wire not_1_out, not_2_out, not_3_out, not_4_out;

  not not_1 (not_1_out, select0);
  not not_2 (not_2_out, select1);
  not not_3 (not_3_out, select1);
  not not_4 (not_4_out, select0);
  and and_1 (output0, not_1_out, not_2_out);
  and and_2 (output1, select0, not_3_out);
  and and_3 (output2, not_4_out, select1);
  and and_4 (output3, select0, select1);
endmodule
