// Logisim project Assignment 5.circ as structural Verilog: 2 circuits, main circuit main
module main (
  input  [4:0] in_1,
  input  [31:0] in_2,
  input  [31:0] in_3,
  output [31:0] out_4,
  output out_5
);

  wire add_slt_1_stl, undriven;
  wire [31:0] add_slt_1_sum, and_1_out, bit_extender_1_out, multiplexer_1_out, multiplexer_2_out, not_1_out,
       not_2_out, or_1_out;

  assign not_1_out = ~in_2;  // NOT_Gate not_1, 32 bits wide
  assign not_2_out = ~in_3;  // NOT_Gate not_2, 32 bits wide
  Multiplexer #(.width(32)) multiplexer_1 (
    .in0(in_2), .in1(not_1_out), .out(multiplexer_1_out), .sel(in_1[4]));  // open: en
  Multiplexer #(.width(32)) multiplexer_2 (
    .in0(in_3), .in1(not_2_out), .out(multiplexer_2_out), .sel(in_1[3]));  // open: en
  assign and_1_out = multiplexer_1_out & multiplexer_2_out;  // AND_Gate and_1, 32 bits wide
  assign or_1_out = multiplexer_1_out | multiplexer_2_out;  // OR_Gate or_1, 32 bits wide
  add_slt add_slt_1 (
    .A(multiplexer_1_out), .B(multiplexer_2_out), .Carry_in(in_1[2]), .Zero(out_5), .Sum(add_slt_1_sum),
    .STL(add_slt_1_stl));
  Multiplexer #(.select(2), .width(32)) multiplexer_3 (
    .in0(and_1_out), .in1(or_1_out), .in2(add_slt_1_sum), .in3(bit_extender_1_out), .out(out_4),
    .sel(in_1[1:0]), .en(undriven));
  assign bit_extender_1_out = {{31{1'b0}}, add_slt_1_stl};  // Bit_Extender bit_extender_1
endmodule

module add_slt (
  input  Carry_in,
  input  [31:0] A,
  input  [31:0] B,
  output Zero,
  output [31:0] Sum,
  output STL
);

  wire adder_1_cout, or_1_out, or_2_out, or_3_out, or_4_out, or_5_out, or_6_out, or_7_out;

  Adder #(.width(31)) adder_1 (.a(A[30:0]), .b(B[30:0]), .out(Sum[30:0]), .cin(Carry_in), .cout(adder_1_cout));
  Adder #(.width(1)) adder_2 (.a(A[31]), .b(B[31]), .out(STL), .cin(adder_1_cout));  // open: cout
  or or_1 (or_1_out, Sum[0], Sum[1], Sum[2], Sum[3], Sum[4]);
  or or_2 (or_2_out, Sum[5], Sum[6], Sum[7], Sum[8], Sum[9]);
  or or_3 (or_3_out, or_1_out, or_2_out, or_4_out, or_5_out, or_6_out);
  or or_4 (or_4_out, Sum[10], Sum[11], Sum[12], Sum[13], Sum[14]);
  or or_5 (or_5_out, Sum[15], Sum[16], Sum[17], Sum[18], Sum[19]);
  or or_6 (or_6_out, Sum[20], Sum[21], Sum[22], Sum[23], Sum[24]);
  or or_7 (or_7_out, Sum[25], Sum[26], Sum[27], Sum[28], Sum[29]);
  nor nor_1 (Zero, or_3_out, or_7_out, Sum[30], STL);

  assign Sum[31] = STL;
endmodule
