// Logisim project Assignment 6.circ as structural Verilog
module ALUControl (
  input  [1:0] ALUOp,
  input  [5:0] Func,
  output [3:0] ALUcon
);

  wire and_1_out, not_1_out, not_2_out, not_3_out, or_1_out;

  or or_1 (or_1_out, Func[0], Func[3]);
  and and_1 (and_1_out, Func[1], ALUOp[1]);
  not not_1 (not_1_out, Func[2]);
  not not_2 (not_2_out, ALUOp[1]);
  not not_3 (not_3_out, ALUOp[0]);
  and and_2 (ALUcon[0], ALUOp[1], or_1_out);
  or or_2 (ALUcon[1], not_1_out, not_2_out);
  or or_3 (ALUcon[2], ALUOp[0], and_1_out);
  and and_3 (ALUcon[3], ALUOp[0], not_3_out);
endmodule

module Main_Control (
  input  [5:0] Op,
  output branch,
  output RegDst,
  output MemRead,
  output MemToReg,
  output [1:0] ALUOp,
  output MemWrite,
  output ALUSrc,
  output RegWrite
);

  wire not_1_out, not_2_out, not_3_out, not_4_out, not_5_out, not_6_out, not_7_out, not_8_out, not_9_out,
       not_10_out, not_11_out, not_12_out, not_13_out, not_14_out, not_15_out, not_16_out;

  not not_1 (not_1_out, Op[0]);
  not not_2 (not_2_out, Op[1]);
  not not_3 (not_3_out, Op[2]);
  not not_4 (not_4_out, Op[3]);
  not not_5 (not_5_out, Op[4]);
  not not_6 (not_6_out, Op[5]);
  not not_7 (not_7_out, Op[2]);
  not not_8 (not_8_out, Op[3]);
  not not_9 (not_9_out, Op[4]);
  not not_10 (not_10_out, Op[2]);
  not not_11 (not_11_out, Op[4]);
  not not_12 (not_12_out, Op[0]);
  not not_13 (not_13_out, Op[1]);
  not not_14 (not_14_out, Op[3]);
  not not_15 (not_15_out, Op[4]);
  not not_16 (not_16_out, Op[5]);
  and and_1 (ALUOp[1], not_1_out, not_2_out, not_3_out, not_4_out, not_5_out, not_6_out);
  and and_2 (MemRead, Op[0], Op[1], not_7_out, not_8_out, not_9_out, Op[5]);
  and and_3 (MemWrite, Op[0], Op[1], not_10_out, Op[3], not_11_out, Op[5]);
  and and_4 (ALUOp[0], not_12_out, not_13_out, Op[2], not_14_out, not_15_out, not_16_out);
  or or_1 (ALUSrc, MemRead, MemWrite);
  or or_2 (RegWrite, ALUOp[1], MemRead);

  assign branch = ALUOp[0];
  assign MemToReg = MemRead;
  assign RegDst = ALUOp[1];
endmodule
