// Logisim project MIPS.circ as structural Verilog: 1 circuit, main circuit main
module main (
);

  wire ALU_out_5, and_1_out, clock_1_out, Control_alusrc, Control_branch, Control_memread, Control_memtoreg,
       Control_memwrite, Control_regdst, Control_regwrite, or_1_out;
  wire [1:0] Control_aluop;
  wire [3:0] ALUControl_alucon;
  wire [4:0] multiplexer_1_out;
  wire [31:0] adder_1_out, adder_2_out, ALU_out_4, bit_extender_1_out, multiplexer_2_out, multiplexer_3_out,
       multiplexer_4_out, PC_q, ram_1_data, register_file_read_data_1, register_file_read_data_2, rom_1_data,
       shifter_1_out;

  Register #(.width(32)) PC (.D(multiplexer_3_out), .en(clock_1_out), .Q(PC_q), .clk(clock_1_out));  // open: clr
  Adder #(.width(32)) adder_1 (.a(PC_q), .b(32'h4), .out(adder_1_out));  // open: cin, cout
  ROM #(.addrWidth(6), .dataWidth(32)) rom_1 (.addr(PC_q[7:2]), .data(rom_1_data));  // open: sel
  Main_Control Control (
    .Op(rom_1_data[31:26]), .branch(Control_branch), .RegDst(Control_regdst), .MemRead(Control_memread),
    .MemToReg(Control_memtoreg), .ALUOp(Control_aluop), .MemWrite(Control_memwrite), .ALUSrc(Control_alusrc),
    .RegWrite(Control_regwrite));
  Multiplexer #(.width(5), .enable("false")) multiplexer_1 (
    .in0(rom_1_data[20:16]), .in1(rom_1_data[15:11]), .out(multiplexer_1_out), .sel(Control_regdst));
  assign bit_extender_1_out = {{16{rom_1_data[15]}}, rom_1_data[15:0]};  // Bit_Extender bit_extender_1
  Clock clock_1 (.out(clock_1_out));
  Register_File_main register_file (
    .read_port_1(rom_1_data[25:21]), .read_port_2(rom_1_data[20:16]), .write_port(multiplexer_1_out),
    .in_5(multiplexer_4_out), .write_enable(Control_regwrite), .clock(clock_1_out),
    .read_data_1(register_file_read_data_1), .read_data_2(register_file_read_data_2));
  ALUControl ALUControl (.Func(rom_1_data[5:0]), .ALUOp(Control_aluop), .ALUcon(ALUControl_alucon));
  Shifter #(.width(32)) shifter_1 (.in(bit_extender_1_out), .\dist (5'b00010), .out(shifter_1_out));
  Multiplexer #(.width(32), .enable("false")) multiplexer_2 (
    .in0(register_file_read_data_2), .in1(bit_extender_1_out), .out(multiplexer_2_out), .sel(Control_alusrc));
  ALU_main ALU (
    .in_2(register_file_read_data_1), .in_3(multiplexer_2_out), .in_1(ALUControl_alucon), .out_4(ALU_out_4),
    .out_5(ALU_out_5));
  Adder #(.width(32)) adder_2 (.a(adder_1_out), .b(shifter_1_out), .out(adder_2_out));  // open: cin, cout
  and and_1 (and_1_out, Control_branch, ALU_out_5);
  or or_1 (or_1_out, Control_memwrite, Control_memread);
  Multiplexer #(.width(32), .enable("false")) multiplexer_3 (
    .in0(adder_1_out), .in1(adder_2_out), .out(multiplexer_3_out), .sel(and_1_out));
  RAM #(.addrWidth(6), .dataWidth(32), .bus("separate")) ram_1 (
    .addr(ALU_out_4[7:2]), .din(register_file_read_data_2), .data(ram_1_data), .str(Control_memwrite),
    .sel(or_1_out), .clk(clock_1_out), .ld(Control_memread));  // open: clr
  Multiplexer #(.width(32), .enable("false")) multiplexer_4 (
    .in0(ALU_out_4), .in1(ram_1_data), .out(multiplexer_4_out), .sel(Control_memtoreg));

  // Notes on the sheet:
  //   instruction memory
  //   contents of rom_1 (hex, n*v repeats v):
  //   22 8c010000 8c020004 8c030008 842022 822020 43282a 10a00002 411020 1000fffb ac040000 1000ffff
  //   shift left 2
  //   data memory
endmodule
