// Logisim project Register File.circ as structural Verilog: 1 circuit, main circuit main
module main (
  input  write_enable,
  input  [4:0] read_port_1,
  input  [4:0] read_port_2,
  input  [4:0] write_port,
  input  [31:0] in_5,
  input  clock,
  output [31:0] read_data_1,
  output [31:0] read_data_2
);

  wire and_1_out, and_2_out, and_3_out, and_4_out, and_5_out, and_6_out, and_7_out, and_8_out,
       decoder_1_out0, decoder_1_out1, decoder_1_out2, decoder_1_out3, decoder_1_out4, decoder_1_out5,
       decoder_1_out6, decoder_1_out7;
  wire [31:0] register_1_q, register_2_q, register_3_q, register_4_q, register_5_q, register_6_q,
       register_7_q, register_8_q;

  Decoder #(.select(3), .enable("false")) decoder_1 (
    .out0(decoder_1_out0), .out1(decoder_1_out1), .out2(decoder_1_out2), .out3(decoder_1_out3),
    .out4(decoder_1_out4), .out5(decoder_1_out5), .out6(decoder_1_out6), .out7(decoder_1_out7),
    .sel(write_port[2:0]));
  and and_1 (and_1_out, decoder_1_out0, write_enable);
  and and_2 (and_2_out, decoder_1_out1, write_enable);
  and and_3 (and_3_out, decoder_1_out2, write_enable);
  and and_4 (and_4_out, decoder_1_out3, write_enable);
  and and_5 (and_5_out, decoder_1_out4, write_enable);
  and and_6 (and_6_out, decoder_1_out5, write_enable);
  and and_7 (and_7_out, decoder_1_out6, write_enable);
  and and_8 (and_8_out, decoder_1_out7, write_enable);
  Register #(.width(32)) register_1 (.D(in_5), .en(and_1_out), .Q(register_1_q), .clk(clock));  // open: clr
  Register #(.width(32)) register_2 (.D(in_5), .en(and_2_out), .Q(register_2_q), .clk(clock));  // open: clr
  Register #(.width(32)) register_3 (.D(in_5), .en(and_3_out), .Q(register_3_q), .clk(clock));  // open: clr
  Register #(.width(32)) register_4 (.D(in_5), .en(and_4_out), .Q(register_4_q), .clk(clock));  // open: clr
  Register #(.width(32)) register_5 (.D(in_5), .en(and_5_out), .Q(register_5_q), .clk(clock));  // open: clr
  Register #(.width(32)) register_6 (.D(in_5), .en(and_6_out), .Q(register_6_q), .clk(clock));  // open: clr
  Register #(.width(32)) register_7 (.D(in_5), .en(and_7_out), .Q(register_7_q), .clk(clock));  // open: clr
  Register #(.width(32)) register_8 (.D(in_5), .en(and_8_out), .Q(register_8_q), .clk(clock));  // open: clr
  Multiplexer #(.select(3), .width(32), .enable("false")) multiplexer_1 (
    .in0(register_1_q), .in1(register_2_q), .in2(register_3_q), .in3(register_4_q), .in4(register_5_q),
    .in5(register_6_q), .in6(register_7_q), .in7(register_8_q), .out(read_data_1), .sel(read_port_1[2:0]));
  Multiplexer #(.select(3), .width(32), .enable("false")) multiplexer_2 (
    .in0(register_1_q), .in1(register_2_q), .in2(register_3_q), .in3(register_4_q), .in4(register_5_q),
    .in5(register_6_q), .in6(register_7_q), .in7(register_8_q), .out(read_data_2), .sel(read_port_2[2:0]));
endmodule
